// Logisim project 1220646_1220429_1221618 .circ as structural Verilog
module ALU (
  input  [31:0] ALU_input1,
  input  [31:0] ALU_input2,
  input  [3:0] OP,
  output [31:0] ALUresult
);

  wire comparator_1_eq, comparator_2_lt;
  wire [31:0] adder_1_out, AND_out, bit_extender_1_out, bit_extender_2_out, CAND_out, not_1_out, OR_out,
       shifter_1_out, shifter_2_out, shifter_3_out, shifter_4_out, subtractor_1_out, XOR_out;

  Comparator #(.width(32)) comparator_1 (.a(ALU_input1), .b(ALU_input2), .eq(comparator_1_eq));  // open: gt, lt
  Comparator #(.width(32)) comparator_2 (.a(ALU_input1), .b(ALU_input2), .lt(comparator_2_lt));  // open: gt, eq
  assign not_1_out = ~ALU_input1;  // NOT_Gate not_1, 32 bits wide
  Adder #(.width(32)) adder_1 (.a(ALU_input1), .b(ALU_input2), .out(adder_1_out));  // open: cin, cout
  assign bit_extender_1_out = {{31{1'b0}}, comparator_1_eq};  // Bit_Extender bit_extender_1
  Subtractor #(.width(32)) subtractor_1 (.a(ALU_input2), .b(ALU_input1), .out(subtractor_1_out));  // open: bin, bout
  assign XOR_out = ALU_input1 ^ ALU_input2;  // XOR_Gate XOR, 32 bits wide
  assign AND_out = ALU_input1 & ALU_input2;  // AND_Gate AND, 32 bits wide
  assign OR_out = ALU_input1 | ALU_input2;  // OR_Gate OR, 32 bits wide
  assign CAND_out = not_1_out & ALU_input2;  // AND_Gate CAND, 32 bits wide
  assign bit_extender_2_out = {{31{1'b0}}, comparator_2_lt};  // Bit_Extender bit_extender_2
  Shifter #(.width(32), .shift("ar")) shifter_1 (.in(ALU_input1), .\dist (ALU_input2[4:0]), .out(shifter_1_out));
  Shifter #(.width(32), .shift("lr")) shifter_2 (.in(ALU_input1), .\dist (ALU_input2[4:0]), .out(shifter_2_out));
  Shifter #(.width(32)) shifter_3 (.in(ALU_input1), .\dist (ALU_input2[4:0]), .out(shifter_3_out));
  Shifter #(.width(32), .shift("rr")) shifter_4 (.in(ALU_input1), .\dist (ALU_input2[4:0]), .out(shifter_4_out));
  Multiplexer #(.select(4), .width(32), .enable("false")) multiplexer_1 (
    .in0(XOR_out), .in1(AND_out), .in2(OR_out), .in3(CAND_out), .in4(adder_1_out), .in5(bit_extender_1_out),
    .in6(subtractor_1_out), .in7(bit_extender_2_out), .in8(shifter_1_out), .in9(shifter_2_out),
    .in10(shifter_3_out), .in11(shifter_4_out), .out(ALUresult), .sel(OP));  // open: in12, in13, in14, in15

  // Other names for the same wires on the sheet: input1[31:0] = ALU_input1; input2[31:0] = ALU_input2

  // Notes on the sheet:
  //   ADD
  //   SEQ
  //   NADD
  //   SLT
  //   SRA
  //   SRL
  //   SLL
  //   ROR
endmodule

module RFile (
  input  [31:0] BusX,
  input  [2:0] Ry,
  input  [2:0] Rz,
  input  [2:0] Rx,
  input  CLK,
  input  RigWrite,
  output [31:0] BusY,
  output [31:0] BusZ
);

  wire and_1_out, and_2_out, and_3_out, and_4_out, and_5_out, and_6_out, and_7_out, decoder_1_out0,
       decoder_1_out1, decoder_1_out2, decoder_1_out3, decoder_1_out4, decoder_1_out5, decoder_1_out6,
       decoder_1_out7, decoder_2_out0, decoder_2_out1, decoder_2_out2, decoder_2_out3, decoder_2_out4,
       decoder_2_out5, decoder_2_out6, decoder_2_out7, decoder_3_out0, decoder_3_out1, decoder_3_out2,
       decoder_3_out3, decoder_3_out4, decoder_3_out5, decoder_3_out6, decoder_3_out7;
  wire [31:0] R1_q, R2_q, R3_q, R4_q, R5_q, R6_q, R7_q;

  Decoder #(.select(3), .enable("false")) decoder_1 (
    .out0(decoder_1_out0), .out1(decoder_1_out1), .out2(decoder_1_out2), .out3(decoder_1_out3),
    .out4(decoder_1_out4), .out5(decoder_1_out5), .out6(decoder_1_out6), .out7(decoder_1_out7), .sel(Rx));
  and and_1 (and_1_out, decoder_1_out1, RigWrite);
  and and_2 (and_2_out, decoder_1_out2, RigWrite);
  and and_3 (and_3_out, decoder_1_out3, RigWrite);
  and and_4 (and_4_out, decoder_1_out4, RigWrite);
  and and_5 (and_5_out, decoder_1_out5, RigWrite);
  and and_6 (and_6_out, decoder_1_out6, RigWrite);
  and and_7 (and_7_out, decoder_1_out7, RigWrite);
  Register #(.width(32)) R1 (.D(BusX), .en(and_1_out), .Q(R1_q), .clk(CLK));  // open: clr
  Register #(.width(32)) R2 (.D(BusX), .en(and_2_out), .Q(R2_q), .clk(CLK));  // open: clr
  Register #(.width(32)) R3 (.D(BusX), .en(and_3_out), .Q(R3_q), .clk(CLK));  // open: clr
  Register #(.width(32)) R4 (.D(BusX), .en(and_4_out), .Q(R4_q), .clk(CLK));  // open: clr
  Register #(.width(32)) R5 (.D(BusX), .en(and_5_out), .Q(R5_q), .clk(CLK));  // open: clr
  Register #(.width(32)) R6 (.D(BusX), .en(and_6_out), .Q(R6_q), .clk(CLK));  // open: clr
  Register #(.width(32)) R7 (.D(BusX), .en(and_7_out), .Q(R7_q), .clk(CLK));  // open: clr
  assign BusY = decoder_2_out0 ? {32{1'b0}} : 32'bz;  // Controlled_Buffer controlled_buffer_1
  Decoder #(.select(3), .enable("false")) decoder_2 (
    .out0(decoder_2_out0), .out1(decoder_2_out1), .out2(decoder_2_out2), .out3(decoder_2_out3),
    .out4(decoder_2_out4), .out5(decoder_2_out5), .out6(decoder_2_out6), .out7(decoder_2_out7), .sel(Ry));
  assign BusY = decoder_2_out1 ? R1_q : 32'bz;  // Controlled_Buffer controlled_buffer_2
  assign BusY = decoder_2_out2 ? R2_q : 32'bz;  // Controlled_Buffer controlled_buffer_3
  assign BusY = decoder_2_out3 ? R3_q : 32'bz;  // Controlled_Buffer controlled_buffer_4
  assign BusY = decoder_2_out4 ? R4_q : 32'bz;  // Controlled_Buffer controlled_buffer_5
  assign BusY = decoder_2_out5 ? R5_q : 32'bz;  // Controlled_Buffer controlled_buffer_6
  assign BusY = decoder_2_out6 ? R6_q : 32'bz;  // Controlled_Buffer controlled_buffer_7
  assign BusY = decoder_2_out7 ? R7_q : 32'bz;  // Controlled_Buffer controlled_buffer_8
  Decoder #(.select(3), .enable("false")) decoder_3 (
    .out0(decoder_3_out0), .out1(decoder_3_out1), .out2(decoder_3_out2), .out3(decoder_3_out3),
    .out4(decoder_3_out4), .out5(decoder_3_out5), .out6(decoder_3_out6), .out7(decoder_3_out7), .sel(Rz));
  assign BusZ = decoder_3_out0 ? {32{1'b0}} : 32'bz;  // Controlled_Buffer controlled_buffer_9
  assign BusZ = decoder_3_out1 ? R1_q : 32'bz;  // Controlled_Buffer controlled_buffer_10
  assign BusZ = decoder_3_out2 ? R2_q : 32'bz;  // Controlled_Buffer controlled_buffer_11
  assign BusZ = decoder_3_out3 ? R3_q : 32'bz;  // Controlled_Buffer controlled_buffer_12
  assign BusZ = decoder_3_out4 ? R4_q : 32'bz;  // Controlled_Buffer controlled_buffer_13
  assign BusZ = decoder_3_out5 ? R5_q : 32'bz;  // Controlled_Buffer controlled_buffer_14
  assign BusZ = decoder_3_out6 ? R6_q : 32'bz;  // Controlled_Buffer controlled_buffer_15
  assign BusZ = decoder_3_out7 ? R7_q : 32'bz;  // Controlled_Buffer controlled_buffer_16
endmodule

module SingleCycleProssesor (
);

  wire _0, _1, _2, _3, _4, _20_out, _21_out, and_1_out, and_2_out, and_3_out, and_4_out, and_5_out,
       and_6_out, and_7_out, and_8_out, branchSelect, CLK_out, equal, ExtOp, greater, greaterThanOrEqual,
       jumpSwl, lessThan, MemRead, MemWrite, not_1_out, not_2_out, not_3_out, not_5_out, not_6_out,
       not_7_out, not_8_out, not_10_out, not_11_out, not_12_out, not_13_out, not_14_out, not_15_out,
       not_16_out, not_17_out, notequal, RegDst, RegWrite;
  wire [1:0] BSel, f, WBdata;
  wire [2:0] Imm3, multiplexer_2_out;
  wire [3:0] ALUOp;
  wire [4:0] shifter_1_out;
  wire [4:2] Imm5;
  wire [7:5] Imm11;
  wire [10:0] shifter_2_out, shifter_3_out;
  wire [19:0] adder_1_out, adder_2_out, bit_extender_1_out, bit_extender_2_out, multiplexer_1_out, pc, PC___2;
  wire [31:0] alu_1_aluresult, bit_extender_5_out, bit_extender_7_out, multiplexer_3_out, multiplexer_4_out,
       multiplexer_5_out, ram_1_data, rfile_1_busy, rfile_1_busz, sExtImm5, SImm11, zExtImm5;

  not not_1 (not_1_out, _3);
  Shifter #(.width(5)) shifter_1 (.in({Imm5, f}), .\dist (3'b001), .out(shifter_1_out));
  and and_1 (and_1_out, and_2_out, greaterThanOrEqual);
  and and_2 (and_2_out, _4, not_1_out, not_2_out, not_3_out, _0);
  not not_2 (not_2_out, _2);
  not not_3 (not_3_out, _1);
  not not_4 (greaterThanOrEqual, lessThan);
  assign bit_extender_1_out = {{15{shifter_1_out[4]}}, shifter_1_out};  // Bit_Extender bit_extender_1
  Shifter #(.width(11)) shifter_2 (.in({Imm3, Imm11, Imm5, f}), .\dist (4'b0001), .out(shifter_2_out));
  Comparator #(.width(3)) comparator_1 (.a(Imm3), .b(Imm11), .gt(greater), .eq(equal), .lt(lessThan));
  Adder #(.width(20)) adder_1 (.a(pc), .b(bit_extender_1_out), .out(adder_1_out));  // open: cin, cout
  assign bit_extender_2_out = {{9{shifter_2_out[10]}}, shifter_2_out};  // Bit_Extender bit_extender_2
  or or_1 (branchSelect, and_1_out, and_3_out, and_5_out, and_7_out);
  and and_3 (and_3_out, and_4_out, lessThan);
  and and_4 (and_4_out, _4, not_7_out, not_5_out, not_6_out, not_8_out);
  not not_5 (not_5_out, _2);
  not not_6 (not_6_out, _1);
  not not_7 (not_7_out, _3);
  not not_8 (not_8_out, _0);
  not not_9 (notequal, equal);
  Adder #(.width(20)) adder_2 (.a(pc), .b(bit_extender_2_out), .out(adder_2_out));  // open: cin, cout
  not not_10 (not_10_out, _4);
  Adder #(.width(20)) adder_3 (.a(pc), .b(20'h2), .out(PC___2));  // open: cin, cout
  Multiplexer #(.select(2), .width(20), .enable("false")) multiplexer_1 (
    .in0(PC___2), .in1(adder_1_out), .in2(adder_2_out), .out(multiplexer_1_out), .sel({jumpSwl, branchSelect}));  // open: in3
  and and_5 (and_5_out, and_6_out, notequal);
  and and_6 (and_6_out, not_10_out, _3, _2, _1, _0);
  and and_7 (and_7_out, and_8_out, equal);
  and and_8 (and_8_out, not_12_out, _3, _2, _1, not_11_out);
  not not_11 (not_11_out, _0);
  not not_12 (not_12_out, _4);
  Register #(.width(20)) u_PC (.D(multiplexer_1_out), .en(1'b1), .Q(pc), .clk(CLK_out));  // open: clr
  Clock CLK (.out(CLK_out));
  ROM #(.addrWidth(20), .dataWidth(16)) rom_1 (
    .addr(pc), .data({_4, _3, _2, _1, _0, Imm3, Imm11, Imm5, f}));  // open: sel
  not not_13 (not_13_out, _3);
  and _21 (_21_out, _4, not_13_out, _2, not_14_out, _0);
  not not_14 (not_14_out, _1);
  Multiplexer #(.width(3), .enable("false")) multiplexer_2 (
    .in0(Imm3), .in1(3'b111), .out(multiplexer_2_out), .sel(RegDst));
  Shifter #(.width(11)) shifter_3 (.in({Imm3, Imm11, Imm5, f}), .\dist (4'b0001), .out(shifter_3_out));
  or or_2 (jumpSwl, _21_out, _20_out);
  not not_15 (not_15_out, _3);
  RFile rfile_1 (
    .BusX(multiplexer_5_out), .Ry(Imm11), .Rz(Imm5), .Rx(multiplexer_2_out), .BusY(rfile_1_busy),
    .RigWrite(RegWrite), .BusZ(rfile_1_busz), .CLK(CLK_out));
  assign zExtImm5 = {{27{1'b0}}, {Imm5, f}};  // Bit_Extender bit_extender_3
  assign sExtImm5 = {{27{Imm5[4]}}, {Imm5, f}};  // Bit_Extender bit_extender_4
  assign bit_extender_5_out = {{27{Imm3[2]}}, {Imm3, f}};  // Bit_Extender bit_extender_5
  assign SImm11 = {{21{shifter_3_out[10]}}, shifter_3_out};  // Bit_Extender bit_extender_6
  and _20 (_20_out, _4, not_15_out, _2, not_16_out, not_17_out);
  not not_16 (not_16_out, _1);
  not not_17 (not_17_out, _0);
  Multiplexer #(.width(32), .enable("false")) multiplexer_3 (
    .in0(zExtImm5), .in1(sExtImm5), .out(multiplexer_3_out), .sel(ExtOp));
  Multiplexer #(.select(2), .width(32), .enable("false")) multiplexer_4 (
    .in0(rfile_1_busz), .in1(multiplexer_3_out), .in2(bit_extender_5_out), .in3(SImm11),
    .out(multiplexer_4_out), .sel(BSel));
  ALU alu_1 (.ALU_input1(rfile_1_busy), .ALU_input2(multiplexer_4_out), .ALUresult(alu_1_aluresult), .OP(ALUOp));
  controlUnit controlunit_1 (
    .opCode({_4, _3, _2, _1, _0}), .f(f), .RBData(WBdata), .memRead(MemRead), .memWrite(MemWrite),
    .bSel(BSel), .extop(ExtOp), .regWrite(RegWrite), .regDes(RegDst), .aluOp(ALUOp));
  RAM #(.addrWidth(20), .dataWidth(32), .bus("separate")) ram_1 (
    .addr(alu_1_aluresult[19:0]), .din(rfile_1_busz), .data(ram_1_data), .str(MemWrite), .clk(CLK_out),
    .ld(MemRead));  // open: sel, clr
  assign bit_extender_7_out = {{12{PC___2[19]}}, PC___2};  // Bit_Extender bit_extender_7
  Multiplexer #(.select(2), .width(32), .enable("false")) multiplexer_5 (
    .in0(alu_1_aluresult), .in1(ram_1_data), .in2(bit_extender_7_out), .out(multiplexer_5_out), .sel(WBdata));  // open: in3

  // Other names for the same wires on the sheet: Imm11 (some bits) = {Imm3, Imm5, f}; Z[2:0] = Imm5; Y[2:0] = Imm11;
  //   op[4:0] = {_4, _3, _2, _1, _0}; Imm2[1:0] = f; Imm5[1:0] = f; joiner[4:0] = {Imm3, f}; X[2:0] = Imm3;
  //   pcselect[1:0] = {jumpSwl, branchSelect}

  // Notes on the sheet:
  //   InstructionMemory
  //   contents of rom_1 (hex, n*v repeats v):
  //   a004
  //   DataMemory
endmodule

module controlUnit (
  input  [4:0] opCode,
  input  [1:0] f,
  output [1:0] RBData,
  output memRead,
  output memWrite,
  output [1:0] bSel,
  output extop,
  output regWrite,
  output regDes,
  output [3:0] aluOp
);

  ROM #(.addrWidth(5), .dataWidth(9)) rom_1 (
    .addr(opCode), .data({regDes, regWrite, extop, bSel, memWrite, memRead, RBData}));  // open: sel
  ROM #(.addrWidth(7), .dataWidth(4)) rom_2 (.addr({f, opCode}), .data(aluOp));  // open: sel

  // Notes on the sheet:
  //   contents of rom_1 (hex, n*v repeats v):
  //   80 80 4*90 4*d0 4*90 4*52 d1 9 49 33 73 1b3 1f3
  //   contents of rom_2 (hex, n*v repeats v):
  //   1 3 2 0 4 6 5 7 4*1 4*3 4*2 4*0 4*4 4*6 4*5 4*7 4*a 4*9 4*8 4*b
endmodule
